# Fritzing sketch question_game_breadboard (saved by Fritzing 1.0.7)
stripboards: 1

parts:
  A2 = Waveshare ESP32-S3 ETH
  J5 = Camdenboss CTB0158-3 [part_number=CTB0158-3 package=THT]
  J6 = Camdenboss CTB0158-3 [part_number=CTB0158-3 package=THT]
  J7 = Camdenboss CTB0158-2 [part_number=CTB0158-2 package=THT]
  J8 = Camdenboss CTB0158-3 [part_number=CTB0158-3 package=THT]
  R6 = Resistor [tolerance=±5% resistance=100 package="0402 [SMD]"]
  R7 = Resistor [tolerance=±5% resistance=100 package="0402 [SMD]"]
  R8 = Resistor [tolerance=±5% resistance=100 package="0402 [SMD]"]
  R9 = Resistor [tolerance=±5% resistance=100 package="0402 [SMD]"]
  R10 = Resistor [tolerance=±5% resistance=100 package="0402 [SMD]"]
  R11 = Resistor [tolerance=±5% resistance=100 package="0402 [SMD]"]
  J9 = Camdenboss CTB0158-2 [part_number=CTB0158-2 package=THT]
  J10 = Camdenboss CTB0158-2 [part_number=CTB0158-2 package=THT]
  R12 = Resistor [tolerance=±5% resistance=100k package="0402 [SMD]"]
  R13 = Resistor [tolerance=±5% resistance=100k package="0402 [SMD]"]
  R14 = Resistor [tolerance=±5% resistance=100k package="0402 [SMD]"]
  R15 = Resistor [tolerance=±5% resistance=10k package="0402 [SMD]"]
  R16 = Resistor [tolerance=±5% resistance=10k package="0402 [SMD]"]
  R17 = Resistor [tolerance=±5% resistance=10k package="0402 [SMD]"]

nets:
  N1: A2.Pin_3, A2.Pin_8, A2.Pin_13, A2.Pin_18, A2.Pin_23, A2.Pin_28, A2.Pin_33, A2.Pin_38, J5.pin2, J6.pin2, J7.pin2, J8.pin2, J9.pin2, J10.pin2, R12.Pin_1, R13.Pin_1, R14.Pin_1
  N2: A2.Pin_4, R11.Pin_1
  N3: A2.Pin_5, R10.Pin_1
  N4: A2.Pin_12, R9.Pin_1
  N5: A2.Pin_14, R8.Pin_1
  N6: A2.Pin_17, R7.Pin_1
  N7: A2.Pin_19, R6.Pin_1
  N8: A2.Pin_25, J10.pin1, R12.Pin_0, R15.Pin_1
  N9: A2.Pin_26, J9.pin1, R13.Pin_0, R16.Pin_1
  N10: A2.Pin_27, J7.pin1, R14.Pin_0, R17.Pin_1
  N11: A2.Pin_36, R15.Pin_0, R16.Pin_0, R17.Pin_0
  N12: J5.pin1, R8.Pin_0
  N13: J5.pin3, R9.Pin_0
  N14: J6.pin1, R10.Pin_0
  N15: J6.pin3, R11.Pin_0
  N16: J8.pin1, R6.Pin_0
  N17: J8.pin3, R7.Pin_0

custom parts:
  Waveshare ESP32-S3 ETH: ESP32-S3 ETH Development Board, 10/100Mbps RJ45 Ethernet port, Wi-Fi &Bluetooth Support, 240MHz Dual Core Processor, ESP32 Ethernet Development Board.
