# Fritzing sketch question_game_schematic (saved by Fritzing 1.0.7)
breadboards: 1

parts:
  R_Pulldown_1 = Resistor [tolerance=±5% power=0.25W resistance=100000 package=THT]
  R_Known_1 = Resistor [tolerance=±5% power=0.25W resistance=10000 package=THT]
  R_Mystery_1 = Resistor [tolerance=±5% power=0.25W resistance=1000 package=THT]
  Waveshare_ESP32-S3 = Adafruit Feather RP2040 SCORPIO [part_number=#5650]
  R_Mystery_2 = Resistor [tolerance=±5% power=0.25W resistance=2200 package=THT]
  R_Pulldown_2 = Resistor [tolerance=±5% power=0.25W resistance=100000 package=THT]
  R_Known_2 = Resistor [tolerance=±5% power=0.25W resistance=10000 package=THT]
  R_Mystery_3 = Resistor [tolerance=±5% power=0.25W resistance=4700 package=THT]
  R_Pulldown_3 = Resistor [tolerance=±5% power=0.25W resistance=100000 package=THT]
  R_Known_3 = Resistor [tolerance=±5% power=0.25W resistance=10000 package=THT]
  LED1 = DUO LED RG [package="5 mm [THT]"]
  R_G1 = Resistor [tolerance=±5% power=0.25W resistance=100 package=THT]
  R_R1 = Resistor [tolerance=±5% power=0.25W resistance=100 package=THT]
  LED2 = DUO LED RG [package="5 mm [THT]"]
  R_G2 = Resistor [tolerance=±5% power=0.25W resistance=100 package=THT]
  R_R2 = Resistor [tolerance=±5% power=0.25W resistance=100 package=THT]
  LED3 = DUO LED RG [package="5 mm [THT]"]
  R_G3 = Resistor [tolerance=±5% power=0.25W resistance=100 package=THT]
  R_R3 = Resistor [tolerance=±5% power=0.25W resistance=100 package=THT]
  R_Mystery_4 = Resistor [tolerance=±5% power=0.25W resistance=10000 package=THT]
  R_Mystery_5 = Resistor [tolerance=±5% power=0.25W resistance=22000 package=THT]
  R_Mystery_6 = Resistor [tolerance=±5% power=0.25W resistance=33000 package=THT]
  R_Mystery_7 = Resistor [tolerance=±5% power=0.25W resistance=47000 package=THT]
  R_Mystery_8 = Resistor [tolerance=±5% power=0.25W resistance=68000 package=THT]
  R_Mystery_9 = Resistor [tolerance=±5% power=0.25W resistance=100000 package=THT]

nets:
  N1: R_Pulldown_1.Pin_0, R_Known_1.Pin_0, R_Mystery_1.Pin_0, Waveshare_ESP32-S3.A0
  GND: R_Pulldown_1.Pin_1, R_Mystery_1.Pin_1, Waveshare_ESP32-S3.GND, R_Mystery_2.Pin_1, R_Pulldown_2.Pin_1, R_Mystery_3.Pin_1, R_Pulldown_3.Pin_1, LED1.common_cathode, LED2.common_cathode, LED3.common_cathode, R_Mystery_4.Pin_1, R_Mystery_5.Pin_1, R_Mystery_6.Pin_1, R_Mystery_7.Pin_1, R_Mystery_8.Pin_1, R_Mystery_9.Pin_1
  3.3V: R_Known_1.Pin_1, Waveshare_ESP32-S3.+3V3, R_Known_2.Pin_1, R_Known_3.Pin_1
  N2: Waveshare_ESP32-S3.A2, R_Mystery_3.Pin_0, R_Pulldown_3.Pin_0, R_Known_3.Pin_0
  N3: Waveshare_ESP32-S3.A1, R_Mystery_2.Pin_0, R_Pulldown_2.Pin_0, R_Known_2.Pin_0
  N4: Waveshare_ESP32-S3.D13, R_R1.Pin_0
  N5: Waveshare_ESP32-S3.D12, R_G1.Pin_0
  N6: Waveshare_ESP32-S3.D11, R_R2.Pin_0
  N7: Waveshare_ESP32-S3.D10, R_G2.Pin_0
  N8: Waveshare_ESP32-S3.D9, R_R3.Pin_0
  N9: Waveshare_ESP32-S3.D6, R_G3.Pin_0
  N10: LED1.red_anode, R_R1.Pin_1
  N11: LED1.green_anode, R_G1.Pin_1
  N12: LED2.red_anode, R_R2.Pin_1
  N13: LED2.green_anode, R_G2.Pin_1
  N14: LED3.red_anode, R_R3.Pin_1
  N15: LED3.green_anode, R_G3.Pin_1
