# Fritzing sketch Protoboard (saved by Fritzing 1.0.7)
circuit board: 8.46667cm x 5.64444cm
stripboards: 1

parts:
  A1 = Waveshare ESP32-S3 ETH
  J1 = Camdenboss CTB0158-2 [part_number=CTB0158-2 package=THT]
  J2 = Camdenboss CTB0158-3 [part_number=CTB0158-3 package=THT]
  J3 = Camdenboss CTB0158-3 [part_number=CTB0158-3 package=THT]
  J4 = Camdenboss CTB0158-3 [part_number=CTB0158-3 package=THT]
  J5 = Camdenboss CTB0158-2 [part_number=CTB0158-2 package=THT]
  J6 = Camdenboss CTB0158-2 [part_number=CTB0158-2 package=THT]
  R1 = Resistor [tolerance=±5% resistance=100 package="0402 [SMD]"]
  R2 = Resistor [tolerance=±5% resistance=100 package="0402 [SMD]"]
  R3 = Resistor [tolerance=±5% resistance=100 package="0402 [SMD]"]
  R4 = Resistor [tolerance=±5% resistance=100 package="0402 [SMD]"]
  R5 = Resistor [tolerance=±5% resistance=100 package="0402 [SMD]"]
  R6 = Resistor [tolerance=±5% resistance=100 package="0402 [SMD]"]
  R7 = Resistor [tolerance=±5% resistance=10k package="0402 [SMD]"]
  R8 = Resistor [tolerance=±5% resistance=100k package="0402 [SMD]"]
  R9 = Resistor [tolerance=±5% resistance=100k package="0402 [SMD]"]
  R10 = Resistor [tolerance=±5% resistance=10k package="0402 [SMD]"]
  R11 = Resistor [tolerance=±5% resistance=10k package="0402 [SMD]"]
  R12 = Resistor [tolerance=±5% resistance=100k package="0402 [SMD]"]

nets:
  N1: A1.Pin_3, A1.Pin_8, A1.Pin_13, A1.Pin_18, A1.Pin_23, A1.Pin_28, A1.Pin_33, A1.Pin_38, J1.pin2, J2.pin2, J3.pin2, J4.pin2, J5.pin2, J6.pin2, R8.Pin_1, R9.Pin_1, R12.Pin_1
  N2: A1.Pin_4, R3.Pin_1
  N3: A1.Pin_5, R6.Pin_1
  N4: A1.Pin_12, R4.Pin_1
  N5: A1.Pin_14, R5.Pin_1
  N6: A1.Pin_17, R1.Pin_1
  N7: A1.Pin_19, R2.Pin_1
  N8: A1.Pin_25, J6.pin1, R7.Pin_0, R8.Pin_0
  N9: A1.Pin_26, J5.pin1, R11.Pin_1, R12.Pin_0
  N10: A1.Pin_27, J1.pin1, R9.Pin_0, R10.Pin_1
  N11: A1.Pin_36, R7.Pin_1, R10.Pin_0, R11.Pin_0
  N12: J2.pin1, R5.Pin_0
  N13: J2.pin3, R4.Pin_0
  N14: J3.pin1, R6.Pin_0
  N15: J3.pin3, R3.Pin_0
  N16: J4.pin1, R2.Pin_0
  N17: J4.pin3, R1.Pin_0

custom parts:
  Waveshare ESP32-S3 ETH: ESP32-S3 ETH Development Board, 10/100Mbps RJ45 Ethernet port, Wi-Fi &Bluetooth Support, 240MHz Dual Core Processor, ESP32 Ethernet Development Board.
